# Fritzing sketch RPI DHT11 (saved by Fritzing 1.0.1rc)

parts:
  J1 = DHT11 basic temperature-humidity sensor [form="♂ (male)" package=THT]
  Raspberry_Pi_1 = Raspberry Pi 3 [part_number=RPI-3-V1.2]

nets:
  VCC: J1.VCC, Raspberry_Pi_1.3v3
  N1: J1.OUT, Raspberry_Pi_1.GIPO23
  GND: J1.GND, Raspberry_Pi_1.GND

custom parts:
  DHT11 basic temperature-humidity sensor: The DHT11 is a basic, ultra low-cost digital temperature and humidity sensor. It uses a capacitive humidity sensor and a thermistor to measure the surrounding air, and spits out a digital signal on the data pin (no analog input pins needed). Its fairly simple to use, but requires careful timing to grab data. The only real downside of this sensor is you can only get new data from it once every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
