# Fritzing sketch RPI RS485 DHT11 (saved by Fritzing 1.0.1rc)

parts:
  Raspberry_Pi_1 = Raspberry Pi 3 [part_number=RPI-3-V1.2]  # not connected
  Componente1 = Arduino Uno (Rev3) - ICSP
  J1 = DHT11 basic temperature-humidity sensor [form="♂ (male)" package=THT]
  M1 = MAX485 Breakout [package=THT]  # not connected
  M2 = MAX485 Breakout [package=THT]  # not connected

nets:
  GND: Componente1.GND, J1.GND
  N1: Componente1.D2, J1.OUT
  5V: Componente1.5V, J1.VCC

custom parts:
  DHT11 basic temperature-humidity sensor: The DHT11 is a basic, ultra low-cost digital temperature and humidity sensor. It uses a capacitive humidity sensor and a thermistor to measure the surrounding air, and spits out a digital signal on the data pin (no analog input pins needed). Its fairly simple to use, but requires careful timing to grab data. The only real downside of this sensor is you can only get new data from it once every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
  MAX485 Breakout: MAX485 RS485 breakout board
